// Logisim project memory_game.circ as structural Verilog: 1 circuit, main circuit main
module main (
);

  Hex_Digit_Display hex_digit_display_1 ();  // open: value, dp
  Hex_Digit_Display hex_digit_display_2 ();  // open: value, dp
  DotMatrix #(.matrixrows(5)) dotmatrix_1 ();  // open: col0, col1, col2, col3, col4
  DotMatrix #(.matrixrows(5)) dotmatrix_2 ();  // open: col0, col1, col2, col3, col4
  DotMatrix #(.matrixrows(5)) dotmatrix_3 ();  // open: col0, col1, col2, col3, col4
  DotMatrix #(.matrixrows(5)) dotmatrix_4 ();  // open: col0, col1, col2, col3, col4
  DotMatrix #(.matrixrows(5)) dotmatrix_5 ();  // open: col0, col1, col2, col3, col4
  DotMatrix #(.matrixrows(5)) dotmatrix_6 ();  // open: col0, col1, col2, col3, col4
  Button button_1 ();  // open: out
  Button button_2 ();  // open: out
  Button button_3 ();  // open: out
  Button button_4 ();  // open: out
  Button button_5 ();  // open: out
  Button button_6 ();  // open: out
  Hex_Digit_Display hex_digit_display_3 ();  // open: value, dp
  DotMatrix #(.matrixrows(5)) dotmatrix_7 ();  // open: col0, col1, col2, col3, col4
  DotMatrix #(.matrixrows(5)) dotmatrix_8 ();  // open: col0, col1, col2, col3, col4
  Button button_7 ();  // open: out
  Button button_8 ();  // open: out
  Button button_9 ();  // open: out
  Button button_10 ();  // open: out
  Hex_Digit_Display hex_digit_display_4 ();  // open: value, dp
  DotMatrix #(.matrixrows(5)) dotmatrix_9 ();  // open: col0, col1, col2, col3, col4
  DotMatrix #(.matrixrows(5)) dotmatrix_10 ();  // open: col0, col1, col2, col3, col4
endmodule
